// Logisim project control-logic.circ as structural Verilog: 1 circuit, main circuit control_logic
module control_logic (
  input  [31:0] inst,
  input  BrEq,
  input  BrLt,
  input  [3:0] in_4,
  output PCSel,
  output RegWEn,
  output [2:0] ImmSel,
  output BrUn,
  output ASel,
  output BSel,
  output [3:0] ALUSel,
  output MemRW,
  output [1:0] WBSel,
  output CSRSel,
  output CSRWen
);

  wire and_3_out, is_SB_or_is_jalr, is_U_type, is_UJ, is_UJ_type, or_3_out, or_4_out;
  wire [2:0] bit_extender_1_out;

  assign bit_extender_1_out = {{2{1'b0}}, inst[3]};  // Bit_Extender bit_extender_1
  assign ImmSel = bit_extender_1_out | inst[6:4];  // OR_Gate or_1, 3 bits wide
  Priority_Encoder priority_encoder_1 ();  // open: in0, in1, in2, in3, in4, in5, in6, in7, out, en_in, gs, en_out
  // Probe on ImmSel
  and and_1 (is_SB_or_is_jalr, inst[0], inst[1], inst[2], ~inst[3], ~inst[4], inst[5], inst[6]);  // AND_Gate
  and and_2 (is_UJ, inst[0], inst[1], inst[2], inst[3], ~inst[4], inst[5], inst[6]);  // AND_Gate
  or or_2 (PCSel, is_SB_or_is_jalr, is_UJ);
  or or_3 (or_3_out, MemRW, is_SB_or_is_jalr);
  not not_1 (RegWEn, or_3_out);
  and and_3 (and_3_out, inst[13], inst[14]);
  and and_4 (is_U_type, inst[0], inst[1], inst[2], ~inst[3], inst[4], inst[5], ~inst[6]);  // AND_Gate
  and and_5 (is_UJ_type, inst[0], inst[1], inst[2], inst[3], ~inst[4], inst[5], inst[6]);  // AND_Gate
  and and_6 (BSel, inst[0], inst[1], ~inst[2], ~inst[3], inst[4], inst[5], ~inst[6]);  // AND_Gate
  and and_7 (MemRW, inst[0], inst[1], ~inst[2], ~inst[3], ~inst[4], inst[5], ~inst[6]);  // AND_Gate
  and and_8 (BrUn, is_SB_or_is_jalr, and_3_out);
  or or_4 (or_4_out, is_SB_or_is_jalr, is_UJ_type, is_U_type);
  not not_2 (ASel, or_4_out);

  assign ALUSel = in_4;
  // also tied to VCC on the sheet: RegWEn

  // Other names for the same wires on the sheet: opcode[6:0] = inst[6:0]; rd[4:0] = inst[11:7];
  //   funct3[2:0] = inst[14:12]; rs1[4:0] = inst[19:15]; imm[11:0] = inst[31:20]; rs2[4:0] = inst[24:20];
  //   funct7[6:0] = inst[31:25]; immed[6:0] = inst[31:25]; is_R_type = BSel; is_S_type = MemRW;
  //   is_SB_type = is_SB_or_is_jalr

  // Notes on the sheet:
  //   I-type: 000,0011
  //   U-type: 001,0111
  //   S-type: 010,0011
  //   R-type: 011,0011; no imm
  //   SB-type: 110,0011
  //   UJ-type: 110,1111
  //   INPUTS to your circuit
  //   ImmSel generator logic
  //   while writting ImmSel, Rtype does not contain imm, so Rtype would not be included.
  //   there is another way to design this circuit, refer to cnblogs: 16225150 
  //   DON'T CHANGE THE LOCATIONS OF THE INPUTS AND OUTPUTS!
  //   OUTPUT from your circuit
  //   the rightest 2 bit always be 1 in these instruction, so this 2 bit would not be contained. becasue this 2 bit cannot identify instrcut type
  //   the highest(leftest) bits shows a regularity. Itype-> 000, Utype->001, Stype->010, SBType-> 110, UJType->110
  //   these 3bits cannot distinct UJ/SB type only, but the 3rd bit is 1 only in UJType. so we can make OR between highest 3bits and extended 3rd bit, to produce a regularity 3bits
  //   THIS CONTROL LOGIC CONTAINS HARD-WIRTED CIRCUIT, BECAUSE THIS PROJECT TEST FEW OF INSTRUCTIOS ONLY
  //   PCSel
  //   BrUn
endmodule
